# Fritzing sketch rpi-pico-onair-bulb (saved by Fritzing 1.0.3b)

parts:
  Mod1 = Raspberry Pi Pico W
  S1 = SWITCH-MOMENTARY-2 [package=tactile-pth-12mm]
  Part1 = 4x Matrix LED 8x8 with MAX7219 [part_number=FC-16]

nets:
  N1: Mod1.pin_4, Part1.CLK
  N2: Mod1.pin_5, Part1.DIN
  N3: Mod1.pin_6, S1.1
  N4: Mod1.pin_7, Part1.CS
  N5: Mod1.pin_8, Mod1.pin_33, Mod1.pin_38, Mod1.pin_42, S1.2, Part1.GND
  N6: Mod1.pin_40, Part1.VCC

custom parts:
  Raspberry Pi Pico W: Raspberry Pi Pico W. Based around the RP2040 microcontroller the Pico W is a low cost microcontroller device bringing Raspberry Pi quality, cost, and easy of use to the microcontroller space. The areas marked KEEPOUT in pcb silkscreen should not have traces running through them to avoid shorts on a soldered in module!
  4x Matrix LED 8x8 with MAX7219: FC-16
